# Fritzing sketch MatrixBoy (saved by Fritzing 0.9.3b)
circuit board: 13.6551cm x 10.2252cm
breadboards: 2

parts:
  Composant1 = Arduino Nano (Rev3.0) (ICSP)
  SPKR1 = Loudspeaker
  Disp1 = LBT2088AH [part_number=LBT2088AH]

nets:
  N1: Composant1.GND, SPKR1.pin1
  N2: Composant1.D2, Disp1.pin_9
  N3: Composant1.D3, Disp1.pin_7
  N4: Composant1.D4, Disp1.pin_8
  N5: Composant1.D5, Disp1.pin_6
  N6: Composant1.D6, Disp1.pin1
  N7: Composant1.D7, Disp1.pin2
  N8: Composant1.D8, Disp1.pin_10
  N9: Composant1.D9, Disp1.pin_5
  N10: Composant1.D10, Disp1.pin_4
  N11: Composant1.D11/MOSI, SPKR1.pin2
  N12: Composant1.D12/MISO, Disp1.pin_3
  N13: Composant1.A5, Disp1.pin_11
  N14: Composant1.A4, Disp1.pin_12
  N15: Composant1.A3, Disp1.pin_13
  N16: Composant1.A2, Disp1.pin_14
  N17: Composant1.A1, Disp1.pin_15
  N18: Composant1.A0, Disp1.pin_16
